# Fritzing sketch planche test (saved by Fritzing 0.9.3b)
breadboards: 1

parts:
  LED1 = RGB LED - (4 legs) [package="5 mm [THT]"]
  LED2 = RGB LED - (4 legs) [package="5 mm [THT]"]
  LED3 = RGB LED - (4 legs) [package="5 mm [THT]"]
  LED6 = RGB LED - (4 legs) [package="5 mm [THT]"]
  R1 = Resistor [tolerance=±5% resistance=220 package=THT]
  R2 = Resistor [tolerance=±5% resistance=220 package=THT]
  R3 = Resistor [tolerance=±5% resistance=220 package=THT]
  R4 = Resistor [tolerance=±5% resistance=220 package=THT]
  R5 = Resistor [tolerance=±5% resistance=220 package=THT]
  R6 = Resistor [tolerance=±5% resistance=220 package=THT]
  R7 = Resistor [tolerance=±5% resistance=220 package=THT]
  R8 = Resistor [tolerance=±5% resistance=220 package=THT]
  R9 = Resistor [tolerance=±5% resistance=220 package=THT]
  R10 = Resistor [tolerance=±5% resistance=220 package=THT]
  R11 = Resistor [tolerance=±5% resistance=220 package=THT]
  R12 = Resistor [tolerance=±5% resistance=220 package=THT]
  Composant1 = Arduino Uno (Rev3)
  LED7 = RGB LED - (4 legs) [package="5 mm [THT]"]
  R19 = Resistor [tolerance=±5% resistance=220 package=THT]
  R20 = Resistor [tolerance=±5% resistance=220 package=THT]
  R21 = Resistor [tolerance=±5% resistance=220 package=THT]
  U1 = ENCODER_2LED [package=encoder_led_2]

nets:
  N1: LED1.red_cathode, R1.Pin_1
  N2: LED1.green_cathode, R7.Pin_1
  N3: LED1.blue_cathode, R6.Pin_1
  N4: LED2.red_cathode, R10.Pin_1
  N5: LED2.green_cathode, R11.Pin_1
  N6: LED2.blue_cathode, R12.Pin_1
  N7: LED3.red_cathode, R3.Pin_0, R5.Pin_1, Composant1.D6_PWM
  N8: LED3.common_anode, LED6.common_anode, Composant1.5V, LED7.common_anode, U1.A
  N9: LED3.green_cathode, R4.Pin_1
  N10: LED6.red_cathode, R2.Pin_1
  N11: LED6.green_cathode, R8.Pin_1
  N12: LED6.blue_cathode, R9.Pin_1
  N13: R1.Pin_0, R5.Pin_0, Composant1.D3_PWM
  N14: R2.Pin_0, R10.Pin_0, Composant1.D9_PWM
  N15: R4.Pin_0, R7.Pin_0, Composant1.D5_PWM
  N16: R8.Pin_0, R11.Pin_0, Composant1.D10_PWM/SS
  N17: R9.Pin_0, R12.Pin_0, Composant1.D11_PWM/MOSI
  N18: Composant1.D8, R19.Pin_0
  N19: Composant1.GND, U1.+R
  N20: Composant1.D0/RX, U1.B
  N21: Composant1.D1/TX, U1.C
  N22: Composant1.D2, U1.-
  N23: Composant1.D4, R21.Pin_0
  N24: Composant1.D7, R20.Pin_0
  N25: LED7.red_cathode, R21.Pin_1
  N26: LED7.green_cathode, R20.Pin_1
  N27: LED7.blue_cathode, R19.Pin_1
